// Logisim project NSU-2023-T04L1e07.circ as structural Verilog: 1 circuit, main circuit mycircuit
module mycircuit (
  input  A,
  input  B,
  input  R,
  input  C
);

  wire xnor_1_out;

  xnor xnor_1 (xnor_1_out, A, C);
  and and_1 (R, xnor_1_out, B);
endmodule
