// Logisim project NSU-2023-T05L2e02.circ as structural Verilog: 1 circuit, main circuit dec
module dec (
  input  [7:0] X,
  output [7:0] R,
  output Cout
);

  assign R = X ^ {1'b1, X[7:1]};  // XOR_Gate xor_1, 8 bits wide

  assign Cout = X[0];
endmodule
